// Logisim project main.circ as structural Verilog
module main (
  input  [7:0] bus_0,
  input  [7:0] bus_0_2,
  input  [7:0] bus_0_3,
  input  [7:0] bus_0_4,
  input  [7:0] bus_0_5,
  input  [7:0] bus_0_6,
  input  [7:0] bus_0_7,
  input  [7:0] bus_0_8
);

  wire clock_1_out, down, flag, left, open, reset, right, up;
  wire [6:0] row_drawer_1__00, row_drawer_1__01, row_drawer_1__02, row_drawer_1__03, row_drawer_1__04,
       row_drawer_1__05, row_drawer_1__06, row_drawer_1__07, row_drawer_1__10, row_drawer_1__11,
       row_drawer_1__12, row_drawer_1__13, row_drawer_1__14, row_drawer_1__15, row_drawer_1__16,
       row_drawer_1__17, row_drawer_1__20, row_drawer_1__21, row_drawer_1__22, row_drawer_1__23,
       row_drawer_1__24, row_drawer_1__25, row_drawer_1__26, row_drawer_1__27, row_drawer_1__30,
       row_drawer_1__31, row_drawer_1__32, row_drawer_1__33, row_drawer_1__34, row_drawer_1__35,
       row_drawer_1__36, row_drawer_1__37, row_drawer_1__40, row_drawer_1__41, row_drawer_1__42,
       row_drawer_1__43, row_drawer_1__44, row_drawer_1__45, row_drawer_1__46, row_drawer_1__47,
       row_drawer_1__50, row_drawer_1__51, row_drawer_1__52, row_drawer_1__53, row_drawer_1__54,
       row_drawer_1__55, row_drawer_1__56, row_drawer_1__57, row_drawer_1__60, row_drawer_1__61,
       row_drawer_1__62, row_drawer_1__63, row_drawer_1__64, row_drawer_1__65, row_drawer_1__66,
       row_drawer_1__67, row_drawer_1__70, row_drawer_1__71, row_drawer_1__72, row_drawer_1__73,
       row_drawer_1__74, row_drawer_1__75, row_drawer_1__76, row_drawer_1__77;

  Button button (.out(up));
  Button v (.out(down));
  Button button_2 (.out(left));
  Button R (.out(reset));
  Button O (.out(open));
  Button button_3 (.out(right));
  Button F (.out(flag));
  Clock clock_1 (.out(clock_1_out));
  row_drawer row_drawer_1 (
    .celll_0(bus_0), ._00(row_drawer_1__00), ._01(row_drawer_1__01), ._02(row_drawer_1__02),
    ._03(row_drawer_1__03), ._04(row_drawer_1__04), ._05(row_drawer_1__05), ._06(row_drawer_1__06),
    ._07(row_drawer_1__07), ._10(row_drawer_1__10), ._11(row_drawer_1__11), ._12(row_drawer_1__12),
    ._13(row_drawer_1__13), ._14(row_drawer_1__14), ._15(row_drawer_1__15), ._16(row_drawer_1__16),
    ._17(row_drawer_1__17), ._20(row_drawer_1__20), ._21(row_drawer_1__21), ._22(row_drawer_1__22),
    ._23(row_drawer_1__23), ._24(row_drawer_1__24), ._25(row_drawer_1__25), ._26(row_drawer_1__26),
    ._27(row_drawer_1__27), .clk(clock_1_out), .cell_1(bus_0_3), .cell_2(bus_0_5), ._30(row_drawer_1__30),
    ._31(row_drawer_1__31), ._32(row_drawer_1__32), .celll_3(bus_0_7), ._33(row_drawer_1__33),
    ._34(row_drawer_1__34), ._35(row_drawer_1__35), ._36(row_drawer_1__36), ._37(row_drawer_1__37),
    ._60(row_drawer_1__60), ._61(row_drawer_1__61), ._62(row_drawer_1__62), .celll_6(bus_0_6),
    ._63(row_drawer_1__63), ._64(row_drawer_1__64), ._65(row_drawer_1__65), ._66(row_drawer_1__66),
    ._67(row_drawer_1__67), ._70(row_drawer_1__70), ._40(row_drawer_1__40), ._71(row_drawer_1__71),
    ._41(row_drawer_1__41), ._72(row_drawer_1__72), ._42(row_drawer_1__42), .celll_7(bus_0_8),
    ._73(row_drawer_1__73), .celll_4(bus_0_2), ._43(row_drawer_1__43), ._74(row_drawer_1__74),
    ._44(row_drawer_1__44), ._75(row_drawer_1__75), ._45(row_drawer_1__45), ._76(row_drawer_1__76),
    ._46(row_drawer_1__46), ._77(row_drawer_1__77), ._47(row_drawer_1__47), ._50(row_drawer_1__50),
    ._51(row_drawer_1__51), ._52(row_drawer_1__52), .celll_5(bus_0_4), ._53(row_drawer_1__53),
    ._54(row_drawer_1__54), ._55(row_drawer_1__55), ._56(row_drawer_1__56), ._57(row_drawer_1__57));
  DotMatrix #(.matrixcols(8)) dotmatrix_1 (
    .col0(row_drawer_1__00), .col1(row_drawer_1__01), .col2(row_drawer_1__02), .col3(row_drawer_1__03),
    .col4(row_drawer_1__04), .col5(row_drawer_1__05), .col6(row_drawer_1__06), .col7(row_drawer_1__07));
  DotMatrix #(.matrixcols(8)) dotmatrix_2 (
    .col0(row_drawer_1__10), .col1(row_drawer_1__11), .col2(row_drawer_1__12), .col3(row_drawer_1__13),
    .col4(row_drawer_1__14), .col5(row_drawer_1__15), .col6(row_drawer_1__16), .col7(row_drawer_1__17));
  DotMatrix #(.matrixcols(8)) dotmatrix_3 (
    .col0(row_drawer_1__20), .col1(row_drawer_1__21), .col2(row_drawer_1__22), .col3(row_drawer_1__23),
    .col4(row_drawer_1__24), .col5(row_drawer_1__25), .col6(row_drawer_1__26), .col7(row_drawer_1__27));
  DotMatrix #(.matrixcols(8)) dotmatrix_4 (
    .col0(row_drawer_1__30), .col1(row_drawer_1__31), .col2(row_drawer_1__32), .col3(row_drawer_1__33),
    .col4(row_drawer_1__34), .col5(row_drawer_1__36), .col6(row_drawer_1__35), .col7(row_drawer_1__37));
  DotMatrix #(.matrixcols(8)) dotmatrix_5 (
    .col0(row_drawer_1__40), .col1(row_drawer_1__41), .col2(row_drawer_1__42), .col3(row_drawer_1__43),
    .col4(row_drawer_1__44), .col5(row_drawer_1__45), .col6(row_drawer_1__46), .col7(row_drawer_1__47));
  DotMatrix #(.matrixcols(8)) dotmatrix_6 (
    .col0(row_drawer_1__50), .col1(row_drawer_1__51), .col2(row_drawer_1__52), .col3(row_drawer_1__53),
    .col4(row_drawer_1__54), .col5(row_drawer_1__55), .col6(row_drawer_1__56), .col7(row_drawer_1__57));
  DotMatrix #(.matrixcols(8)) dotmatrix_7 (
    .col0(row_drawer_1__60), .col1(row_drawer_1__62), .col2(row_drawer_1__63), .col3(row_drawer_1__64),
    .col4(row_drawer_1__65), .col5(row_drawer_1__67), .col6(row_drawer_1__66), .col7(row_drawer_1__70));
  DotMatrix #(.matrixcols(8)) dotmatrix_8 (
    .col0(row_drawer_1__71), .col1(row_drawer_1__72), .col2(row_drawer_1__73), .col3(row_drawer_1__74),
    .col4(row_drawer_1__75), .col5(row_drawer_1__76), .col6(row_drawer_1__77), .col7(row_drawer_1__61));
  controller controller_1 (
    .reset(reset), .up(up), .left(left), .down(down), .right(right), .open(open), .flag(flag));  // open: IRQ, vec
  map_handler map_handler_1 ();
  processor_hadnler processor_hadnler_1 ();  // open: clk
endmodule

module processor_hadnler (
  input  clk
);

  wire data_ins, mem;

  CdM_8_mark5 cdm_8_mark5_1 (
    .clock(clk), .mem_cycle(mem), .data_inst(data_ins));  // open: addr, mem_read, data_out, data_in, r0, r1, r2, r3, PC, SP, PS, IAck, IRQ, vec
endmodule

module map_selector (
  input  bus_0
);

  ROM rom_1 ();  // open: addr, data, sel
  ROM rom_2 ();  // open: addr, data, sel
  ROM rom_3 ();  // open: addr, data, sel
  ROM rom_4 ();  // open: addr, data, sel
  ROM rom_5 ();  // open: addr, data, sel
  ROM rom_6 ();  // open: addr, data, sel
endmodule

module controller (
  input  reset,
  input  up,
  input  left,
  input  down,
  input  right,
  input  open,
  input  flag,
  input  vec,
  output IRQ
);

  Multiplexer #(.select(3)) multiplexer_1 (
    .in0(reset), .in1(up), .in2(left), .in3(down), .in4(right), .in5(open), .in6(flag), .in7(1'b0),
    .out(vec), .en(vec));  // open: sel
  or or_1 (IRQ, reset, up, left, down, right, open, flag);
endmodule

module cell_drawer (
  input  [7:0] cell_data,
  input  clk,
  output [6:0] row_0,
  output [6:0] row_1,
  output [6:0] row_2,
  output [6:0] row_3,
  output [6:0] row_4,
  output [6:0] row_5,
  output [6:0] row_6,
  output explose,
  output [6:0] row_7
);

  wire not_1_out;
  wire [1:0] and_2_out, or_1_out;
  wire [3:0] print;
  wire [6:0] not_2_out, not_3_out, not_4_out, not_5_out, not_6_out, not_7_out, not_8_out, not_9_out, row_0_t,
       row_1_t, row_2_t, row_3_t, row_4_t, row_5_t, row_6_t, row_7_t;
  wire [7:0] cell_data_t;

  and and_1 (explose, cell_data_t[3], cell_data_t[6]);
  // Probe on print
  Multiplexer #(.select(4), .width(7)) multiplexer_1 (
    .in0(7'b0000001), .in1({7{1'b0}}), .in2({7{1'b0}}), .in3({7{1'b0}}), .in4({7{1'b0}}), .in5({7{1'b0}}),
    .in6({7{1'b0}}), .in7({7{1'b0}}), .in8({7{1'b1}}), .in9({7{1'b0}}), .in10({7{1'b0}}), .in11({7{1'b0}}),
    .in12({7{1'b0}}), .in13({7{1'b0}}), .in14({7{1'b0}}), .in15({7{1'b0}}), .out(row_0_t), .sel(print),
    .en(1'b1));
  Multiplexer #(.select(4), .width(7)) multiplexer_2 (
    .in0({7{1'b0}}), .in1(7'b0011110), .in2(7'b0101010), .in3(7'b0101010), .in4(7'b0111110),
    .in5(7'b0101010), .in6(7'b0101010), .in7(7'b0101000), .in8(7'b1000001), .in9(7'b0011100),
    .in10(7'b0111000), .in11({7{1'b0}}), .in12({7{1'b0}}), .in13({7{1'b0}}), .in14({7{1'b0}}),
    .in15({7{1'b0}}), .out(row_4_t), .sel(print), .en(1'b1));
  Register register_1 (.D(cell_data), .Q(cell_data_t), .clk(clk));  // open: en, clr
  // Probe on row_0_t
  and and_2 (and_2_out[0], cell_data_t[3], cell_data_t[6]);
  not not_1 (not_1_out, cell_data_t[3]);
  and and_3 (and_2_out[1], not_1_out, cell_data_t[6]);
  Multiplexer #(.select(4), .width(7)) multiplexer_3 (
    .in0({7{1'b0}}), .in1({7{1'b0}}), .in2({7{1'b0}}), .in3({7{1'b0}}), .in4({7{1'b0}}), .in5({7{1'b0}}),
    .in6({7{1'b0}}), .in7({7{1'b0}}), .in8(7'b1000001), .in9(7'b0100010), .in10({7{1'b0}}), .in11({7{1'b0}}),
    .in12({7{1'b0}}), .in13({7{1'b0}}), .in14({7{1'b0}}), .in15({7{1'b0}}), .out(row_1_t), .sel(print),
    .en(1'b1));
  Multiplexer #(.select(4), .width(7)) multiplexer_4 (
    .in0(7'b1111110), .in1({7{1'b0}}), .in2(7'b0010010), .in3(7'b0010100), .in4(7'b0000100),
    .in5(7'b0100100), .in6(7'b0000100), .in7(7'b0110000), .in8(7'b1000001), .in9(7'b0001000),
    .in10(7'b0111000), .in11({7{1'b0}}), .in12({7{1'b0}}), .in13({7{1'b0}}), .in14({7{1'b0}}),
    .in15({7{1'b0}}), .out(row_5_t), .sel(print), .en(1'b1));
  assign or_1_out = and_2_out | {2{cell_data_t[4]}};  // OR_Gate or_1, 2 bits wide
  // Probe on print
  Multiplexer #(.select(2), .width(4)) multiplexer_5 (
    .in0(4'b1000), .in1(4'b1001), .in2({1'b0, cell_data_t[2:0]}), .in3(4'b1010), .out(print), .sel(or_1_out));  // open: en
  Multiplexer #(.select(4), .width(7)) multiplexer_6 (
    .in0({7{1'b0}}), .in1({7{1'b0}}), .in2(7'b0100110), .in3(7'b0100010), .in4(7'b0001100), .in5(7'b0111010),
    .in6(7'b0011100), .in7(7'b0100000), .in8(7'b1000001), .in9(7'b0001000), .in10(7'b0111111),
    .in11({7{1'b0}}), .in12({7{1'b0}}), .in13({7{1'b0}}), .in14({7{1'b0}}), .in15({7{1'b0}}), .out(row_2_t),
    .sel(print), .en(1'b1));
  Multiplexer #(.select(4), .width(7)) multiplexer_7 (
    .in0({7{1'b0}}), .in1({7{1'b0}}), .in2({7{1'b0}}), .in3({7{1'b0}}), .in4({7{1'b0}}), .in5({7{1'b0}}),
    .in6({7{1'b0}}), .in7({7{1'b0}}), .in8(7'b1000001), .in9(7'b0100010), .in10(7'b0111000),
    .in11({7{1'b0}}), .in12({7{1'b0}}), .in13({7{1'b0}}), .in14({7{1'b0}}), .in15({7{1'b0}}), .out(row_6_t),
    .sel(print), .en(1'b1));
  Multiplexer #(.width(7)) multiplexer_8 (.in0(row_0_t), .in1(not_2_out), .out(row_0), .sel(cell_data_t[5]), .en(1'b1));
  assign not_2_out = ~row_0_t;  // NOT_Gate not_2, 7 bits wide
  Multiplexer #(.width(7)) multiplexer_9 (.in0(row_1_t), .in1(not_3_out), .out(row_1), .sel(cell_data_t[5]), .en(1'b1));
  assign not_3_out = ~row_1_t;  // NOT_Gate not_3, 7 bits wide
  Multiplexer #(.width(7)) multiplexer_10 (
    .in0(row_2_t), .in1(not_4_out), .out(row_2), .sel(cell_data_t[5]), .en(1'b1));
  assign not_4_out = ~row_2_t;  // NOT_Gate not_4, 7 bits wide
  Multiplexer #(.width(7)) multiplexer_11 (
    .in0(row_3_t), .in1(not_5_out), .out(row_3), .sel(cell_data_t[5]), .en(1'b1));
  assign not_5_out = ~row_3_t;  // NOT_Gate not_5, 7 bits wide
  Multiplexer #(.width(7)) multiplexer_12 (
    .in0(row_4_t), .in1(not_6_out), .out(row_4), .sel(cell_data_t[5]), .en(1'b1));
  assign not_6_out = ~row_4_t;  // NOT_Gate not_6, 7 bits wide
  Multiplexer #(.width(7)) multiplexer_13 (
    .in0(row_5_t), .in1(not_7_out), .out(row_5), .sel(cell_data_t[5]), .en(1'b1));
  assign not_7_out = ~row_5_t;  // NOT_Gate not_7, 7 bits wide
  Multiplexer #(.width(7)) multiplexer_14 (
    .in0(row_6_t), .in1(not_8_out), .out(row_6), .sel(cell_data_t[5]), .en(1'b1));
  assign not_8_out = ~row_6_t;  // NOT_Gate not_8, 7 bits wide
  Multiplexer #(.width(7)) multiplexer_15 (
    .in0(row_7_t), .in1(not_9_out), .out(row_7), .sel(cell_data_t[5]), .en(1'b1));
  assign not_9_out = ~row_7_t;  // NOT_Gate not_9, 7 bits wide
  Multiplexer #(.select(4), .width(7)) multiplexer_16 (
    .in0({7{1'b0}}), .in1(7'b0010000), .in2(7'b0101010), .in3(7'b0101010), .in4(7'b0010100),
    .in5(7'b0101010), .in6(7'b0101010), .in7(7'b0100110), .in8(7'b1000001), .in9(7'b0011100),
    .in10(7'b0111000), .in11({7{1'b0}}), .in12({7{1'b0}}), .in13({7{1'b0}}), .in14({7{1'b0}}),
    .in15({7{1'b0}}), .out(row_3_t), .sel(print), .en(1'b1));
  Multiplexer #(.select(4), .width(7)) multiplexer_17 (
    .in0({7{1'b0}}), .in1({7{1'b0}}), .in2({7{1'b0}}), .in3({7{1'b0}}), .in4({7{1'b0}}), .in5({7{1'b0}}),
    .in6({7{1'b0}}), .in7({7{1'b0}}), .in8({7{1'b1}}), .in9({7{1'b0}}), .in10({7{1'b0}}), .in11({7{1'b0}}),
    .in12({7{1'b0}}), .in13({7{1'b0}}), .in14({7{1'b0}}), .in15({7{1'b0}}), .out(row_7_t), .sel(print),
    .en(1'b1));
  DotMatrix #(.matrixcols(1)) dotmatrix_1 (.col0(7'b0100010));

  // Other names for the same wires on the sheet: selected = cell_data_t[5]
endmodule

module row_drawer (
  input  [7:0] celll_6,
  input  [7:0] celll_0,
  input  [7:0] celll_3,
  input  clk,
  input  [7:0] celll_7,
  input  [7:0] cell_1,
  input  [7:0] celll_4,
  input  [7:0] cell_2,
  input  [7:0] celll_5,
  output [6:0] _60,
  output [6:0] _00,
  output [6:0] _30,
  output [6:0] _61,
  output [6:0] _01,
  output [6:0] _31,
  output [6:0] _62,
  output [6:0] _02,
  output [6:0] _32,
  output [6:0] _63,
  output [6:0] _03,
  output [6:0] _33,
  output [6:0] _64,
  output [6:0] _04,
  output [6:0] _34,
  output [6:0] _65,
  output [6:0] _05,
  output [6:0] _35,
  output [6:0] _66,
  output [6:0] _06,
  output [6:0] _36,
  output [6:0] _67,
  output [6:0] _07,
  output [6:0] _37,
  output [6:0] _70,
  output [6:0] _10,
  output [6:0] _40,
  output [6:0] _71,
  output [6:0] _11,
  output [6:0] _41,
  output [6:0] _72,
  output [6:0] _12,
  output [6:0] _42,
  output [6:0] _73,
  output [6:0] _13,
  output [6:0] _43,
  output [6:0] _74,
  output [6:0] _14,
  output [6:0] _44,
  output [6:0] _75,
  output [6:0] _15,
  output [6:0] _45,
  output [6:0] _76,
  output [6:0] _16,
  output [6:0] _46,
  output [6:0] _77,
  output [6:0] _17,
  output [6:0] _47,
  output [6:0] _20,
  output [6:0] _50,
  output [6:0] _21,
  output [6:0] _51,
  output [6:0] _22,
  output [6:0] _52,
  output [6:0] _23,
  output [6:0] _53,
  output [6:0] _24,
  output [6:0] _54,
  output [6:0] _25,
  output [6:0] _55,
  output [6:0] _26,
  output [6:0] _56,
  output [6:0] _27,
  output [6:0] _57
);

  cell_drawer cell_drawer_1 (
    .cell_data(cell_1), .clk(clk), .row_0(_10), .row_1(_11), .row_2(_12), .row_3(_13), .row_4(_14),
    .row_5(_15), .row_6(_16), .row_7(_17));  // open: explose
  cell_drawer cell_drawer_2 (
    .cell_data(cell_2), .clk(clk), .row_0(_20), .row_1(_21), .row_2(_22), .row_3(_23), .row_4(_24),
    .row_5(_25), .row_6(_26), .row_7(_27));  // open: explose
  cell_drawer cell_drawer_3 (
    .cell_data(celll_0), .clk(clk), .row_0(_00), .row_1(_01), .row_2(_02), .row_3(_03), .row_4(_04),
    .row_5(_05), .row_6(_06), .row_7(_07));  // open: explose
  cell_drawer cell_drawer_4 (
    .cell_data(celll_3), .clk(clk), .row_0(_30), .row_1(_31), .row_2(_32), .row_3(_33), .row_4(_34),
    .row_5(_35), .row_6(_36), .row_7(_37));  // open: explose
  cell_drawer cell_drawer_5 (
    .cell_data(celll_4), .clk(clk), .row_0(_40), .row_1(_41), .row_2(_42), .row_3(_43), .row_4(_44),
    .row_5(_45), .row_6(_46), .row_7(_47));  // open: explose
  cell_drawer cell_drawer_6 (
    .cell_data(celll_5), .clk(clk), .row_0(_50), .row_1(_51), .row_2(_52), .row_3(_53), .row_4(_54),
    .row_5(_55), .row_6(_56), .row_7(_57));  // open: explose
  cell_drawer cell_drawer_7 (
    .cell_data(celll_7), .clk(clk), .row_0(_70), .row_1(_71), .row_2(_72), .row_3(_73), .row_4(_74),
    .row_5(_75), .row_6(_76), .row_7(_77));  // open: explose
  cell_drawer cell_drawer_8 (
    .cell_data(celll_6), .clk(clk), .row_0(_60), .row_1(_61), .row_2(_62), .row_3(_63), .row_4(_64),
    .row_5(_65), .row_6(_66), .row_7(_67));  // open: explose
endmodule
